# Fritzing sketch temp_sensor_schema (saved by Fritzing 0.9.3b)
breadboards: 1

parts:
  Composant1 = Arduino Nano (Rev3.0)
  U6 = RF-LINK_TX [package=rf-link_tx]
  R1 = Resistor [tolerance=±5% resistance=220 package="0603 [SMD]"]
  DHT1 = DHT22

nets:
  GND: Composant1.GND, U6.GND, DHT1.GND_2
  N1: Composant1.D2, R1.Pin_0, DHT1.Data-signal
  N2: Composant1.D12/MISO, U6.DATA
  5V: Composant1.5V, R1.Pin_1, DHT1.Vcc
  3V3: Composant1.3V3, U6.+5V

custom parts:
  RF-LINK_TX: Common RF transmitter of the 315.00Mhz varity
  DHT22: Digital relative humidity & temperature sensor DHT22
